# Fritzing sketch CDB (saved by Fritzing 1.0.0d)
circuit board: 9cm x 4cm

parts:
  A1 = GY-NEO6MV2
  A2 = GY-BMP280 Breakout
  J1 = Piezo Speaker
  M3 = RioRand LM2596
  U1 = LIPO-2000mAh [package=lipo-2000]
  RFM95W1 = RFM95W LoRa Module
  J2 = Basic Servo
  M1 = DOIT Esp32 DevKit v1 (30 pins long, 11 pins width) [part_number=ESP32S-PIN30]

nets:
  VCC: A1.Vcc#0, M3.Pin_3, J2.vcc, M1.VIN
  N1: A1.Vcc#1, M1.TX2
  N2: A1.Rx, M1.RX2
  GND: A1.Tx, A2.Pin_2, J1.pin1, M3.Pin_4, RFM95W1.8_GND, RFM95W1.10_GND, RFM95W1.11_DIO3, J2.gnd, M1.GND
  N3: A2.Pin_1, RFM95W1.13_3.3V, M1.3V3
  N4: A2.Pin_3, M1.D22
  N5: A2.Pin_4, M1.D21
  N6: J1.pin2, M1.D15
  N7: M3.Pin_1, U1.+
  N8: M3.Pin_2, U1.-
  N9: RFM95W1.2_MISO, M1.D19
  N10: RFM95W1.3_MOSI, M1.D23
  N11: RFM95W1.4_SCK, M1.D18
  N12: RFM95W1.5_NSS_(CS), M1.D5
  N13: RFM95W1.6_RESET, M1.D14
  N14: RFM95W1.14_DIO0, M1.D4
  N15: J2.pulse, M1.D13

notes:
  Bateria LIPO 3.8V
  Step down regulado para 3.3V

custom parts:
  GY-NEO6MV2: Description: Module GPS , type GY-NEO6MV2, pour arduino et autres micro-contrôleurs. Caractéristiques De type GY-NEO6MV2 Alimentation 3V-5V Avec Flight Control EEPROM MWC Antenne large céramique, fort signal, 25 x 25 mm Paramètres de configuration sauvegardés en EEPROM Avec batterie de backup de données LED témoin de signal Module miniaturisé 25 x 35 mm Trou de fixation de 3mm Baud rate par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
  RFM95W LoRa Module: RF Transceiver by Hope RF. Well supported Arduino libraries are available. This Low Power Long Range Transceiver Module for the frequencies 868MHz and 915MHz and it is also available in other versions. This particular part is set for trhough hole rather than SMD in pcb view.
  DOIT Esp32 DevKit v1 (30 pins long, 11 pins width): The DOIT Esp32 DevKit v1 is one of the development board created by DOIT to evaluate the ESP-WROOM-32 module. It is based on the ESP32 microcontroller that boasts Wifi, Bluetooth, Ethernet and Low Power support all in a single chip. (vanepp) made breadboard work, adjusted pin numbering and labels and reduced size of schematic and cleaned up pcb. This chip is 30pins long (2 x15) and 11 pins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
