# Fritzing sketch Untitled Sketch 2 (saved by Fritzing 1.0.0d)
circuit board: 29.1419cm x 11.4872cm

parts:
  A1 = GY-NEO6MV2
  A2 = GY-BMP280 Breakout
  J1 = Piezo Speaker
  M1 = DOIT Esp32 DevKit v1 (30 pins long, 11 pins width) [part_number=ESP32S-PIN30]
  J2 = Basic Servo
  M2 = RioRand LM2596
  M3 = RioRand LM2596
  Mod1 = 2S-BMS
  SIM800L1 = SIM800L
  R1 = Resistor [tolerance=±5% power=0.25W resistance=2000 package=THT]
  R2 = Resistor [tolerance=±5% power=0.25W resistance=1000 package=THT]
  R3 = Resistor [tolerance=±5% power=0.25W resistance=220 package=THT]

nets:
  VIN: A1.Vcc#0, M1.VIN, J2.vcc, M3.Pin_3
  N1: A1.Vcc#1, M1.TX2
  N2: A1.Rx, M1.RX2
  GND: A1.Tx, A2.Pin_2, J1.pin1, M1.GND, J2.gnd, M2.Pin_4, M3.Pin_4, SIM800L1.GND, R1.Pin_1
  N3: A2.Pin_1, M1.3V3
  N4: A2.Pin_3, M1.D22
  N5: A2.Pin_4, M1.D21
  N6: J1.pin2, R3.Pin_1
  N7: M1.D4, R3.Pin_0
  N8: M1.D18, J2.pulse
  N9: M1.D26, SIM800L1.TXD
  N10: M1.D27, R2.Pin_1
  N11: M2.Pin_1, M3.Pin_1, Mod1.pin1
  N12: M2.Pin_2, M3.Pin_2, Mod1.pin2
  N13: M2.Pin_3, SIM800L1.VCC
  N14: SIM800L1.RXD, R1.Pin_0, R2.Pin_0

custom parts:
  GY-NEO6MV2: Description: Module GPS , type GY-NEO6MV2, pour arduino et autres micro-contrôleurs. Caractéristiques De type GY-NEO6MV2 Alimentation 3V-5V Avec Flight Control EEPROM MWC Antenne large céramique, fort signal, 25 x 25 mm Paramètres de configuration sauvegardés en EEPROM Avec batterie de backup de données LED témoin de signal Module miniaturisé 25 x 35 mm Trou de fixation de 3mm Baud rate par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
  DOIT Esp32 DevKit v1 (30 pins long, 11 pins width): The DOIT Esp32 DevKit v1 is one of the development board created by DOIT to evaluate the ESP-WROOM-32 module. It is based on the ESP32 microcontroller that boasts Wifi, Bluetooth, Ethernet and Low Power support all in a single chip. (vanepp) made breadboard work, adjusted pin numbering and labels and reduced size of schematic and cleaned up pcb. This chip is 30pins long (2 x15) and 11 pins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
  2S-BMS: 2S-BMS LIPO battery charger / protection unit. Note pcb does not match the board as it will likely connect with wires, so pcb is 5 pads suitable for .1in header pins.
  SIM800L: SIM800L is a miniature cellular module which allows for GPRS transmission, sending and receiving SMS and making and receiving voice calls. Low cost and small footprint and quad band frequency support make this module perfect solution for any project that require long range connectivity. After connecting power module boots up, searches for cellular network and login automatically. On board LED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
